# Fritzing sketch Inclinometer_ADXL335_Arduino_Uno (saved by Fritzing 0.9.2b)
circuit board: 18.0293cm x 12.3945cm
breadboards: 1

parts:
  Part1 = Arduino Uno (Rev3)
  Part2 = Triple Axis Accelerometer Breakout - ADXL335
  LCD1 = LCD screen
  BAT1 = BC9VPC [package=bc9vpc]
  R1 = Trimmer Potentiometer [maximum_resistance=10kΩ package=THT]

nets:
  N1: Part1.A3, Part2.ZOUT
  N2: Part1.A4/SDA, Part2.YOUT
  N3: Part1.A5/SCL, Part2.XOUT
  GND: Part1.D8, Part1.GND, Part2.GND, LCD1.VSS, LCD1.RS, LCD1.R/W, LCD1.LED-, BAT1.V-, R1.leg2
  N4: Part1.D9_PWM, LCD1.E
  N5: Part1.D10_PWM/SS, LCD1.DB4
  N6: Part1.D11_PWM/MOSI, LCD1.DB5
  N7: Part1.D12/MISO, LCD1.DB6
  N8: Part1.D13/SCK, LCD1.DB7
  N9: Part1.AREF, Part1.3V3
  5V: Part1.5V, Part2.VCC, LCD1.VDD, LCD1.LED+, R1.leg1
  N10: Part1.VIN, BAT1.V+
  N11: LCD1.V0, R1.wiper
